// Logisim project Lab 7.circ as structural Verilog: 5 circuits, main circuit S-R Latch
module S_R_Latch (
  input  in_1,
  input  in_2,
  output out_3,
  output out_4
);

  wire or_1_out, or_2_out;

  or or_1 (or_1_out, in_1, out_4);
  or or_2 (or_2_out, out_3, in_2);
  not not_1 (out_3, or_1_out);
  not not_2 (out_4, or_2_out);
endmodule

module D_Latch (
  input  in_1,
  input  in_2,
  output out_3
);

  wire and_1_out, and_2_out, not_1_out;

  not not_1 (not_1_out, in_1);
  and and_1 (and_1_out, in_1, in_2);
  and and_2 (and_2_out, not_1_out, in_2);
  S_R_Latch SR (.in_1(and_1_out), .in_2(and_2_out), .out_4(out_3));  // open: out_3

  // Notes on the sheet:
  //   We ignore the NOT Q output
endmodule

module Decoder (
  input  in_1,
  input  in_2,
  output out_3,
  output out_4,
  output out_5,
  output out_6
);

  wire not_1_out, not_2_out, not_3_out, not_4_out;

  not not_1 (not_1_out, in_1);
  not not_2 (not_2_out, in_2);
  not not_3 (not_3_out, in_1);
  not not_4 (not_4_out, in_2);
  and and_1 (out_3, not_1_out, not_2_out);
  and and_2 (out_4, not_3_out, in_2);
  and and_3 (out_5, in_1, not_4_out);
  and and_4 (out_6, in_1, in_2);
endmodule

module RAM (
  input  in_1,
  input  _2Bit_Addr,
  input  in_3,
  input  _3Bit_Data,
  input  in_5,
  input  Read,
  input  Write,
  output out_8,
  output out_9,
  output out_10,
  output out_11,
  output out_12,
  output out_13,
  output out_14,
  output _3_Bit_Out,
  output out_16,
  output out_17,
  output out_18,
  output out_19,
  output out_20,
  output out_21,
  output out_22
);

  wire and_1_out, and_2_out, and_3_out, and_4_out, and_5_out, and_6_out, and_7_out, and_8_out, and_9_out,
       and_10_out, and_11_out, and_12_out, and_13_out, and_14_out, and_15_out, and_16_out, decoder_1_out_3,
       decoder_1_out_4, decoder_1_out_5, decoder_1_out_6;

  Decoder decoder_1 (
    .out_3(decoder_1_out_3), .out_4(decoder_1_out_4), .out_5(decoder_1_out_5), .out_6(decoder_1_out_6),
    .in_1(in_1), .in_2(_2Bit_Addr));
  and and_1 (and_1_out, decoder_1_out_3, Write);
  and and_2 (and_2_out, decoder_1_out_4, Write);
  and and_3 (and_3_out, decoder_1_out_5, Write);
  and and_4 (and_4_out, decoder_1_out_6, Write);
  D_Latch d_latch_1 (.in_1(in_3), .in_2(and_1_out), .out_3(out_8));
  D_Latch d_latch_2 (.in_1(in_3), .in_2(and_2_out), .out_3(out_11));
  D_Latch d_latch_3 (.in_1(in_3), .in_2(and_3_out), .out_3(out_17));
  D_Latch d_latch_4 (.in_1(in_3), .in_2(and_4_out), .out_3(out_20));
  and and_5 (and_5_out, out_8, Read, decoder_1_out_3);
  and and_6 (and_6_out, out_11, decoder_1_out_4, Read);
  and and_7 (and_7_out, out_17, Read, decoder_1_out_5);
  and and_8 (and_8_out, out_20, Read, decoder_1_out_6);
  D_Latch d_latch_5 (.in_1(_3Bit_Data), .in_2(and_1_out), .out_3(out_9));
  D_Latch d_latch_6 (.in_1(_3Bit_Data), .in_2(and_2_out), .out_3(out_12));
  D_Latch d_latch_7 (.in_1(_3Bit_Data), .in_2(and_3_out), .out_3(out_18));
  D_Latch d_latch_8 (.in_1(_3Bit_Data), .in_2(and_4_out), .out_3(out_21));
  and and_9 (and_9_out, out_21, Read, decoder_1_out_6);
  and and_10 (and_10_out, out_9, Read, decoder_1_out_3);
  and and_11 (and_11_out, out_12, decoder_1_out_4, Read);
  and and_12 (and_12_out, out_18, Read, decoder_1_out_5);
  D_Latch d_latch_9 (.in_1(in_5), .in_2(and_1_out), .out_3(out_10));
  D_Latch d_latch_10 (.in_1(in_5), .in_2(and_2_out), .out_3(out_13));
  D_Latch d_latch_11 (.in_1(in_5), .in_2(and_3_out), .out_3(out_19));
  D_Latch d_latch_12 (.in_1(in_5), .in_2(and_4_out), .out_3(out_22));
  and and_13 (and_13_out, out_10, Read, decoder_1_out_3);
  and and_14 (and_14_out, out_13, decoder_1_out_4, Read);
  and and_15 (and_15_out, out_19, Read, decoder_1_out_5);
  and and_16 (and_16_out, out_22, Read, decoder_1_out_6);
  or or_1 (out_14, and_5_out, and_8_out, and_6_out, and_7_out);
  or or_2 (_3_Bit_Out, and_10_out, and_11_out, and_12_out, and_9_out);
  or or_3 (out_16, and_13_out, and_14_out, and_15_out, and_16_out);

  // Notes on the sheet:
  //   Implement  3 Bit, 4 Word RAM
  //   Part 1: Implement the WRITE operation
  //   Part 2: Implement the READ operation. When in WRITE or NONE, the OUTPUT should all be 0s, and when in READ, the output should be the output of the selected addr line
  //   Andrew Chuah and Bhagyesh Patel 
  //   I pledge my honor that I have abided by the Stevens Honor System.
endmodule

module R_W_RAM (
  input  in_1,
  input  _2_Bit_Address,
  input  in_3,
  input  _3_Bit_Data,
  input  in_5,
  input  _1___WRITE,
  input  _1___ENABLED,
  output out_8,
  output OUTPUT,
  output out_10
);

  wire and_1_out, and_2_out, not_1_out;

  not not_1 (not_1_out, _1___WRITE);
  and and_1 (and_1_out, not_1_out, _1___ENABLED);
  and and_2 (and_2_out, _1___WRITE, _1___ENABLED);
  RAM RAM (
    .in_1(in_1), ._2Bit_Addr(_2_Bit_Address), .in_3(in_3), ._3Bit_Data(_3_Bit_Data), .in_5(in_5),
    .Read(and_1_out), .Write(and_2_out), .out_14(out_8), ._3_Bit_Out(OUTPUT), .out_16(out_10));  // open: out_8, out_9, out_10, out_11, out_12, out_13, out_17, out_18, out_19, out_20, out_21, out_22

  // Notes on the sheet:
  //   0 = READ
  //   0 = DISABLED
  //   Have 2 inputs, 1 for ENABLED/DISABLED, and one for READ/WRITE
  //   Part 3: Implement RAM using the RAM you made before, but don't allow the ability to click both READ and WRITE
  //   Andrew Chuah and Bhagyesh Patel
  //   I pledge my honor that I have abided by the Stevens Honor System.
endmodule
